// Logisim project TN1_25520730.circ as structural Verilog: 1 circuit, main circuit main
module main (
  input  A,
  input  B,
  output A1,
  output cAND,
  output cOR,
  output cNAND,
  output cNOR,
  output cXOR,
  output cXNOR
);

  not not_1 (A1, A);
  and and_1 (cAND, A, B);
  or or_1 (cOR, A, B);
  nand nand_1 (cNAND, A, B);
  nor nor_1 (cNOR, A, B);
  xor xor_1 (cXOR, A, B);
  xnor xnor_1 (cXNOR, A, B);
endmodule
